# Fritzing sketch wiring (saved by Fritzing 0.9.2b)
breadboards: 1

parts:
  Raspberry_Pi_1 = Raspberry Pi 3
  R1 = Photocell (LDR) [package=THT]
  C1 = Capacitor [package=cap-pth-small2]
  LED1 = LED - 5mm [color="Red (633nm)" package="5 mm [THT]"]
  LED2 = smd LED [color="Green (560nm)" package="1206 [SMD]"]
  R2 = Resistor [tolerance=±5% resistance=220 package="0402 [SMD]"]
  R3 = Resistor [tolerance=±5% resistance=220 package="0402 [SMD]"]
  R4 = Resistor [tolerance=±5% resistance=220 package="0402 [SMD]"]
  LED3 = smd LED [color="Blue (470nm)" package="1206 [SMD]"]
  LED4 = LED - 5mm [color="Yellow (592nm)" package="5 mm [THT]"]
  R5 = Resistor [tolerance=±5% resistance=220 package="0402 [SMD]"]
  S1 = Magnetic Door Switch [package=reed_switch_plastic]

nets:
  N1: Raspberry_Pi_1.GIPO4, S1.2
  N2: Raspberry_Pi_1.GIPO17, R1.pin_1, C1.1
  N3: Raspberry_Pi_1.GIPO19, LED3.anode
  N4: Raspberry_Pi_1.GIPO26, LED4.anode
  N5: Raspberry_Pi_1.GND, C1.2, R2.Pin_0, R3.Pin_0, R4.Pin_0, R5.Pin_0, S1.1
  N6: Raspberry_Pi_1.GIPO21, LED1.anode
  N7: Raspberry_Pi_1.GIPO20, LED2.anode
  N8: Raspberry_Pi_1.5V, R1.pin_0
  N9: LED1.cathode, R3.Pin_1
  N10: LED2.cathode, R2.Pin_1
  N11: R4.Pin_1, LED3.cathode
  N12: LED4.cathode, R5.Pin_1
